# Fritzing sketch main_circuit (saved by Fritzing 0.9.5d)

parts:
  Power_plug2 = Power plug
  Power_plug5 = USB-C plug
  Power_plug6 = USB-C plug  # not connected
  U1 = 74AHCT125 [part_number=SN74AHCT125 package=dil14]
  LED2 = WS2812 RGB LED strip
  LED1 = WS2812 RGB LED strip
  LED2_2 = WS2812 RGB LED strip
  LED1_2 = WS2812 RGB LED strip
  LED2_3 = WS2812 RGB LED strip
  LED1_3 = WS2812 RGB LED strip
  Power_plug_5v = Power plug
  A1 = Waveshare rp2040-zero tht [package=THT]
  Raspberry_Pi_4B1 = Raspberry Pi 4B
  USBTTL1 = USB A Plug  # not connected

nets:
  GND: Power_plug2.GND, Power_plug5.GND
  VCC: Power_plug2.VCC, Power_plug5.VCC
  GND_2: U1.1OE, U1.2OE, U1.GND, LED2.GND#0, LED1.GND#0, Power_plug_5v.GND, A1.Pin_2, Raspberry_Pi_4B1.GND, Raspberry_Pi_4B1.GPIO24
  N1: U1.1A, A1.Pin_9
  N2: U1.1Y, LED1.DIN
  N3: U1.2A, A1.Pin_8
  N4: U1.2Y, LED2.DIN
  VCC_2: U1.VCC, LED2.VCC#1, LED1.VCC#1, Power_plug_5v.VCC, A1.Pin_1
  N5: LED2.GND#4, LED2_3.GND#0
  N6: LED2.VCC#5, LED2_3.VCC#1
  N7: LED2.DOUT, LED2_3.DIN
  N8: LED1.GND#4, LED1_3.GND#0
  N9: LED1.VCC#5, LED1_3.VCC#1
  N10: LED1.DOUT, LED1_3.DIN
  N11: LED2_2.GND, LED2_3.GND#4
  N12: LED2_2.VCC, LED2_3.VCC#5
  N13: LED2_2.DIN, LED2_3.DOUT
  N14: LED1_2.GND, LED1_3.GND#4
  N15: LED1_2.VCC, LED1_3.VCC#5
  N16: LED1_2.DIN, LED1_3.DOUT
  N17: A1.Pin_18, Raspberry_Pi_4B1.GPIO8, Raspberry_Pi_4B1.GPIO7, Raspberry_Pi_4B1.ID_SC
  N18: A1.Pin_19, Raspberry_Pi_4B1.3V3, Raspberry_Pi_4B1.GPIO10, Raspberry_Pi_4B1.GPIO9, Raspberry_Pi_4B1.GPIO25
  N19: A1.Pin_21, Raspberry_Pi_4B1.GPIO11

notes:
  5 V
  Pico rp2040
  Zero
  Raspberry Pi4 2Gb
  MH-ET Live ESP32
  CH9102X
  - - - - -
  - - - - - - - - - - - - - - - - - - - - - -
  - -
  No connection
  WS2812B

custom parts:
  USB-C plug: power plug
  74AHCT125: Quad Level-Shifter (3V to 5V) Quadruple Bus Buffer Gates With 3-State Outputs
  WS2812 RGB LED strip: WS2812 strip
  Waveshare rp2040-zero tht: .RP2040-Zero, A Low-Cost, High-Performance Pico-Like MCU Board Based On Raspberry Pi Microcontroller RP2040. This varant is THT without the extra connections.
